// Logisim project ElevatorLogic_V11.0.circ as structural Verilog: 13 circuits, main circuit main
module main (
);

  wire CLR, Direction__Up___0, F1, F1_L, F1_UP, F2, F2_DOWN, F2_DOWN_L, F2_L, F2_UP, F2_UP_L, F3, F3_DOWN,
       F3_DOWN_L, F3_L, F3_UP, F3_UP_L, F4, F4_DOWN, F4_DOWN_L, F4_L, F4_UP, F4_UP_L, F5, F5_DOWN, F5_DOWN_L,
       F5_L, F5_UP, F5_UP_L, F6, F6_DOWN, F6_DOWN_L, F6_L, F6_UP, F6_UP_L, F7, F7_DOWN, F7_DOWN_L, F7_L,
       F7_UP, F7_UP_L, F8, F8_DOWN, F8_DOWN_L, F8_L, F8_UP, F8_UP_L, F9, F9_DOWN, F9_DOWN_L, Moving;
  wire [3:0] controlled_buffer_1_out, CURR_FLOOR, NEXT_FLOOR;
  wire [5:0] directiondisplay_1_out_3, directiondisplay_1_out_4, directiondisplay_1_out_5,
       directiondisplay_1_out_6, directiondisplay_1_out_7;

  Button Floor_1 (.out(F1));
  Button Floor_2 (.out(F2));
  Button Floor_3 (.out(F3));
  Button Floor_4 (.out(F4));
  Button Floor_5 (.out(F5));
  Button Floor_6 (.out(F6));
  Button Floor_7 (.out(F7));
  Button Floor_8 (.out(F8));
  Button Floor_9 (.out(F9));
  Button CLEAR (.out(CLR));
  LED led_1 (.in(F1_L));
  LED led_2 (.in(F2_L));
  LED led_3 (.in(F3_L));
  LED led_4 (.in(F4_L));
  LED led_5 (.in(F5_L));
  LED led_6 (.in(F6_L));
  LED led_7 (.in(F7_L));
  LED led_8 (.in(F8_L));
  LED led_9 (.in(F9_DOWN_L));
  Button Floor_1___UP (.out(F1_UP));
  Button Floor_2___DOWN (.out(F2_DOWN));
  Button Floor_2___UP (.out(F2_UP));
  Button Floor_3___DOWN (.out(F3_DOWN));
  Button Floor_3___UP (.out(F3_UP));
  Button Floor_4___DOWN (.out(F4_DOWN));
  Button Floor_4___UP (.out(F4_UP));
  Button Floor_5___DOWN (.out(F5_DOWN));
  Button Floor_5___UP (.out(F5_UP));
  Button Floor_6___DOWN (.out(F6_DOWN));
  Button Floor_6___UP (.out(F6_UP));
  Button Floor_7___DOWN (.out(F7_DOWN));
  Button Floor_7___UP (.out(F7_UP));
  Button Floor_8___DOWN (.out(F8_DOWN));
  Button Floor_8___UP (.out(F8_UP));
  Button Floor_9___DOWN (.out(F9_DOWN));
  LED led_10 (.in(F1_L));
  LED led_11 (.in(F2_DOWN_L));
  LED led_12 (.in(F2_UP_L));
  LED led_13 (.in(F3_DOWN_L));
  LED led_14 (.in(F3_UP_L));
  LED led_15 (.in(F4_DOWN_L));
  LED led_16 (.in(F4_UP_L));
  LED led_17 (.in(F5_DOWN_L));
  LED led_18 (.in(F5_UP_L));
  LED led_19 (.in(F6_DOWN_L));
  LED led_20 (.in(F6_UP_L));
  LED led_21 (.in(F7_DOWN_L));
  LED led_22 (.in(F7_UP_L));
  LED led_23 (.in(F8_DOWN_L));
  LED led_24 (.in(F8_UP_L));
  LED led_25 (.in(F9_DOWN_L));
  DotMatrix #(.matrixrows(6)) dotmatrix_1 (
    .col0(directiondisplay_1_out_3), .col1(directiondisplay_1_out_4), .col2(directiondisplay_1_out_5),
    .col3(directiondisplay_1_out_6), .col4(directiondisplay_1_out_7));
  DirectionDisplay directiondisplay_1 (
    .Direction__0___Up__1___Down(Direction__Up___0), .Moving(Moving), .out_3(directiondisplay_1_out_3),
    .out_4(directiondisplay_1_out_4), .out_5(directiondisplay_1_out_5), .out_6(directiondisplay_1_out_6),
    .out_7(directiondisplay_1_out_7));
  Hex_Digit_Display hex_digit_display_1 (.value(CURR_FLOOR));  // open: dp
  ProcessingUnit processingunit_1 (
    .F1_C(F1), .F2_C(F2), .F3_C(F3), .F4_C(F4), .F5_C(F5), .F6_C(F6), .F7_C(F7), .F8_C(F8), .F9_C(F9),
    .F1_U(F1_UP), .F2_U(F2_UP), .F2_D(F2_DOWN), .F3_U(F3_UP), .F3_D(F3_DOWN), .F4_U(F4_UP), .F4_D(F4_DOWN),
    .F5_U(F5_UP), .F5_D(F5_DOWN), .F6_U(F6_UP), .F6_D(F6_DOWN), .F7_U(F7_UP), .F7_D(F7_DOWN), .F8_U(F8_UP),
    .F8_D(F8_DOWN), .F9_D(F9_DOWN), .CLEAR(CLR), .Current_Floor(CURR_FLOOR), .Next_Floor(NEXT_FLOOR),
    .F1U_LED(F1_L), .F2U_LED(F2_UP_L), .F3U_LED(F3_UP_L), .F4U_LED(F4_UP_L), .F5U_LED(F5_UP_L),
    .F6U_LED(F6_UP_L), .F7U_LED(F7_UP_L), .F8U_LED(F8_UP_L), .F2D_LED(F2_DOWN_L), .F3D_LED(F3_DOWN_L),
    .F4D_LED(F4_DOWN_L), .F5D_LED(F5_DOWN_L), .F6D_LED(F6_DOWN_L), .F7D_LED(F7_DOWN_L), .F8D_LED(F8_DOWN_L),
    .F9D_LED(F9_DOWN_L), .Moving(Moving), .Direction(Direction__Up___0));
  or or_1 (F2_L, F2_UP_L, F2_DOWN_L);
  or or_2 (F3_L, F3_UP_L, F3_DOWN_L);
  or or_3 (F4_L, F4_UP_L, F4_DOWN_L);
  or or_4 (F5_L, F5_UP_L, F5_DOWN_L);
  or or_5 (F6_L, F6_UP_L, F6_DOWN_L);
  or or_6 (F7_L, F7_UP_L, F7_DOWN_L);
  or or_7 (F8_L, F8_UP_L, F8_DOWN_L);
  Hex_Digit_Display hex_digit_display_2 (.value(controlled_buffer_1_out));  // open: dp
  assign controlled_buffer_1_out = Moving ? NEXT_FLOOR : 4'bz;  // Controlled_Buffer controlled_buffer_1

  // Other names for the same wires on the sheet: F1_UP_L = F1_L; F9_L = F9_DOWN_L

  // Notes on the sheet:
  //   INSIDE THE CABIN
  //   OUTSIDE THE CABIN
  //   Direction
  //   ELEVATOR STATUS
  //   Current Floor
  //   Request Processing Unit
  //   Next Floor
endmodule

module ProcessingUnit (
  input  F1_C,
  input  F2_C,
  input  F3_C,
  input  F4_C,
  input  F5_C,
  input  F6_C,
  input  F7_C,
  input  F8_C,
  input  F9_C,
  input  F1_U,
  input  F2_U,
  input  F2_D,
  input  F3_U,
  input  F3_D,
  input  F4_U,
  input  F4_D,
  input  F5_U,
  input  F5_D,
  input  F6_U,
  input  F6_D,
  input  F7_U,
  input  F7_D,
  input  F8_U,
  input  F8_D,
  input  F9_D,
  input  CLEAR,
  output [3:0] Current_Floor,
  output [3:0] Next_Floor,
  output F1U_LED,
  output F2U_LED,
  output F3U_LED,
  output F4U_LED,
  output F5U_LED,
  output F6U_LED,
  output F7U_LED,
  output F8U_LED,
  output F2D_LED,
  output F3D_LED,
  output F4D_LED,
  output F5D_LED,
  output F6D_LED,
  output F7D_LED,
  output F8D_LED,
  output F9D_LED,
  output Moving,
  output Direction
);

  wire and_1_out, and_2_out, and_3_out, and_4_out, and_5_out, and_6_out, and_7_out, and_8_out, and_9_out,
       and_10_out, and_11_out, and_12_out, CLK, comparator_1_eq, comparator_2_eq, comparator_4_eq,
       comparator_5_gt, comparator_5_lt, comparator_6_eq, comparator_7_gt, comparator_7_lt, comparator_8_eq,
       comparator_9_eq, comparator_10_eq, comparator_11_gt, comparator_11_lt, comparator_12_eq,
       comparator_13_gt, comparator_13_lt, comparator_14_eq, comparator_15_eq, controlled_buffer_1_out,
       decoder_1_out0, decoder_1_out1, decoder_1_out2, decoder_1_out3, decoder_2_out5, F1U_L1, F1U_L3,
       F2D_L2, F2D_L4, F2U_L1, F2U_L3, F3D_L2, F3D_L4, F3U_L1, F3U_L3, F4D_L2, F4D_L4, F4U_L1, F4U_L3,
       F5D_L2, F5D_L4, F5U_L1, F5U_L3, F6D_L2, F6D_L4, F6U_L1, F6U_L3, F7D_L2, F7D_L4, F7U_L1, F7U_L3,
       F8D_L2, F8D_L4, F8U_L1, F8U_L3, F9D_L2, F9D_L4, hasStopped, IncrementRH, not_1_out, not_2_out,
       not_3_out, or_1_out, Pop, pull_resistor_1_node, ResetSequencer;
  wire [1:0] RHead;
  wire [2:0] read_sequencer_1_output;
  wire [3:0] DestinationFloor, FloorDownReq, FloorUpReq, IN4, IN_1, IN_2, IN_3, IN_4, multiplexer_1_out,
       MUX_OUT, OUT_1, OUT_2, OUT_3, OUT_4, up_down_counter_1_next_floor;
  wire [4:0] New_Req;

  Clock clock_1 (.out(CLK));
  Comparator #(.width(4), .mode("unsigned")) comparator_1 (
    .a(Current_Floor), .b(4'b0000), .eq(comparator_1_eq));  // open: gt, lt
  Register #(.width(4)) Next_Floor_Reg (.D(DestinationFloor), .Q(Next_Floor), .clk(CLK));  // open: en, clr
  Multiplexer #(.width(4)) multiplexer_1 (
    .in0(up_down_counter_1_next_floor), .in1(4'b0001), .out(multiplexer_1_out), .sel(comparator_1_eq));  // open: en
  Register #(.width(4)) Moving_Floor_Reg (
    .D(multiplexer_1_out), .Q(Current_Floor), .clk(controlled_buffer_1_out));  // open: en, clr
  assign controlled_buffer_1_out = or_1_out ? CLK : 1'bz;  // Controlled_Buffer controlled_buffer_1
  or or_1 (or_1_out, comparator_1_eq, not_1_out);
  Input_Handler input_handler_1 (
    .Current_Floor(Current_Floor), .F1_COP(F1_C), .F2_COP(F2_C), .F3_COP(F3_C), .F4_COP(F4_C), .F5_COP(F5_C),
    .F6_COP(F6_C), .F7_COP(F7_C), .F8_COP(F8_C), .F9_COP(F9_C), .F1_UP(F1_U), .F2_UP(F2_U), .F2_DOWN(F2_D),
    .F3_UP(F3_U), .F3_DOWN(F3_D), .F4_UP(F4_U), .F4_DOWN(F4_D), .F5_UP(F5_U), .F5_DOWN(F5_D), .F6_UP(F6_U),
    .F6_DOWN(F6_D), .F7_UP(F7_U), .F7_DOWN(F7_D), .F8_UP(F8_U), .F8_DOWN(F8_D), .F9_DOWN(F9_D),
    .Request(New_Req));
  not not_1 (not_1_out, hasStopped);
  Hex_Digit_Display hex_digit_display_1 (.value(up_down_counter_1_next_floor));  // open: dp
  Up_Down_Counter up_down_counter_1 (
    .Current_Floor(Current_Floor), .Destination(Next_Floor), .Next_Floor(up_down_counter_1_next_floor),
    .Stop(hasStopped));
  Counter #(.width(2), .max('h3)) counter_1 (.Q(RHead), .clk(IncrementRH));  // open: load, D, count, carry, clr
  Decoder #(.select(2)) decoder_1 (
    .out0(decoder_1_out0), .out1(decoder_1_out1), .out2(decoder_1_out2), .out3(decoder_1_out3), .sel(RHead));  // open: en
  Read_Sequencer read_sequencer_1 (.Start(hasStopped), .Reset(ResetSequencer), .Output(read_sequencer_1_output));
  Multiplexer #(.select(2), .width(4)) multiplexer_2 (
    .in0(OUT_1), .in1(OUT_2), .in2(OUT_3), .in3(OUT_4), .out(MUX_OUT), .sel(RHead));  // open: en
  and and_1 (and_1_out, decoder_1_out0, Pop);
  and and_2 (and_2_out, decoder_1_out2, Pop);
  Decoder #(.select(3), .disabled(0)) decoder_2 (
    .out1(Pop), .out5(decoder_2_out5), .out6(IncrementRH), .sel(read_sequencer_1_output));  // open: out0, out2, out3, out4, out7, en
  RequestStackAscending _1__Up (
    .Pop(and_1_out), .Input(IN_1), .Clear(CLEAR), .Output(OUT_1), .F1_LED(F1U_L1), .F2_LED(F2U_L1),
    .F3_LED(F3U_L1), .F4_LED(F4U_L1), .F5_LED(F5U_L1), .F6_LED(F6U_L1), .F7_LED(F7U_L1), .F8_LED(F8U_L1));  // open: F9_LED
  RequestStackAscending _3__Up (
    .Pop(and_2_out), .Input(IN_3), .Clear(CLEAR), .Output(OUT_3), .F1_LED(F1U_L3), .F2_LED(F2U_L3),
    .F3_LED(F3U_L3), .F4_LED(F4U_L3), .F5_LED(F5U_L3), .F6_LED(F6U_L3), .F7_LED(F7U_L3), .F8_LED(F8U_L3));  // open: F9_LED
  not not_2 (not_2_out, comparator_2_eq);
  Comparator #(.width(4), .mode("unsigned")) comparator_2 (
    .a(MUX_OUT), .b(4'b0000), .eq(comparator_2_eq));  // open: gt, lt
  Pull_Resistor pull_resistor_1 (.node(pull_resistor_1_node));
  Comparator #(.width(4), .mode("unsigned")) comparator_3 (
    .a(MUX_OUT), .b(4'b0000), .eq(pull_resistor_1_node));  // open: gt, lt
  not not_3 (not_3_out, pull_resistor_1_node);
  and and_3 (and_3_out, decoder_1_out1, Pop);
  and and_4 (and_4_out, decoder_1_out3, Pop);
  assign ResetSequencer = decoder_2_out5 ? not_2_out : 1'bz;  // Controlled_Buffer controlled_buffer_2
  Pull_Resistor pull_resistor_2 (.node(ResetSequencer));
  assign DestinationFloor = not_3_out ? MUX_OUT : 4'bz;  // Controlled_Buffer controlled_buffer_3
  RequestStackDescending _2__Down (
    .Pop(and_3_out), .Input(IN_2), .Clear(CLEAR), .Output(OUT_2), .F2_LED(F2D_L2), .F3_LED(F3D_L2),
    .F4_LED(F4D_L2), .F5_LED(F5D_L2), .F6_LED(F6D_L2), .F7_LED(F7D_L2), .F8_LED(F8D_L2), .F9_LED(F9D_L2));  // open: F1_LED
  RequestStackDescending _4__Down (
    .Pop(and_4_out), .Input(IN_4), .Clear(CLEAR), .Output(OUT_4), .F2_LED(F2D_L4), .F3_LED(F3D_L4),
    .F4_LED(F4D_L4), .F5_LED(F5D_L4), .F6_LED(F6D_L4), .F7_LED(F7D_L4), .F8_LED(F8D_L4), .F9_LED(F9D_L4));  // open: F1_LED
  // Probe on FloorUpReq
  // Probe on FloorUpReq
  Comparator #(.width(2), .mode("unsigned")) comparator_4 (.a(RHead), .b(2'b00), .eq(comparator_4_eq));  // open: gt, lt
  // Probe on Current_Floor
  // Probe on Current_Floor
  Comparator #(.width(4), .mode("unsigned")) comparator_5 (
    .a(Current_Floor), .b(FloorUpReq), .gt(comparator_5_gt), .lt(comparator_5_lt));  // open: eq
  and and_5 (and_5_out, comparator_4_eq, comparator_5_lt);
  Pull_Resistor pull_resistor_3 (.node(comparator_5_lt));
  Pull_Resistor pull_resistor_4 (.node(comparator_5_gt));
  Comparator #(.width(2), .mode("unsigned")) comparator_6 (.a(RHead), .b(2'b10), .eq(comparator_6_eq));  // open: gt, lt
  Comparator #(.width(4), .mode("unsigned")) comparator_7 (
    .a(Current_Floor), .b(FloorUpReq), .gt(comparator_7_gt), .lt(comparator_7_lt));  // open: eq
  and and_6 (and_6_out, comparator_6_eq, comparator_7_lt);
  Pull_Resistor pull_resistor_5 (.node(comparator_7_lt));
  Pull_Resistor pull_resistor_6 (.node(comparator_7_gt));
  Comparator #(.width(2), .mode("unsigned")) comparator_8 (.a(RHead), .b(2'b01), .eq(comparator_8_eq));  // open: gt, lt
  Pull_Resistor pull_resistor_7 (.node(comparator_8_eq));
  Comparator #(.width(2), .mode("unsigned")) comparator_9 (.a(RHead), .b(2'b11), .eq(comparator_9_eq));  // open: gt, lt
  Pull_Resistor pull_resistor_8 (.node(comparator_9_eq));
  Demultiplexer #(.width(4)) demultiplexer_1 (
    .out0(FloorUpReq), .out1(FloorDownReq), .in(New_Req[3:0]), .sel(New_Req[4]));  // open: en
  Pull_Resistor pull_resistor_9 (.node(IN_1));
  assign IN_1 = and_5_out ? FloorUpReq : 4'bz;  // Controlled_Buffer controlled_buffer_4
  assign IN_3 = and_7_out ? FloorUpReq : 4'bz;  // Controlled_Buffer controlled_buffer_5
  and and_7 (and_7_out, comparator_4_eq, comparator_5_gt);
  Pull_Resistor pull_resistor_10 (.node(IN_3));
  assign IN_3 = and_6_out ? FloorUpReq : 4'bz;  // Controlled_Buffer controlled_buffer_6
  Pull_Resistor pull_resistor_11 (.node(IN_1));
  assign IN_1 = and_8_out ? FloorUpReq : 4'bz;  // Controlled_Buffer controlled_buffer_7
  and and_8 (and_8_out, comparator_6_eq, comparator_7_gt);
  Pull_Resistor pull_resistor_12 (.node(IN_3));
  assign IN_3 = comparator_8_eq ? FloorUpReq : 4'bz;  // Controlled_Buffer controlled_buffer_8
  Pull_Resistor pull_resistor_13 (.node(IN_1));
  assign IN_1 = comparator_9_eq ? FloorUpReq : 4'bz;  // Controlled_Buffer controlled_buffer_9
  // Probe on FloorDownReq
  // Probe on FloorDownReq
  Comparator #(.width(2), .mode("unsigned")) comparator_10 (
    .a(RHead), .b(2'b01), .eq(comparator_10_eq));  // open: gt, lt
  // Probe on Current_Floor
  Comparator #(.width(4), .mode("unsigned")) comparator_11 (
    .a(Current_Floor), .b(FloorDownReq), .gt(comparator_11_gt), .lt(comparator_11_lt));  // open: eq
  Comparator #(.width(2), .mode("unsigned")) comparator_12 (
    .a(RHead), .b(2'b11), .eq(comparator_12_eq));  // open: gt, lt
  // Probe on Current_Floor
  Comparator #(.width(4), .mode("unsigned")) comparator_13 (
    .a(Current_Floor), .b(FloorDownReq), .gt(comparator_13_gt), .lt(comparator_13_lt));  // open: eq
  Comparator #(.width(2), .mode("unsigned")) comparator_14 (
    .a(RHead), .b(2'b00), .eq(comparator_14_eq));  // open: gt, lt
  Comparator #(.width(2), .mode("unsigned")) comparator_15 (
    .a(RHead), .b(2'b10), .eq(comparator_15_eq));  // open: gt, lt
  and and_9 (and_9_out, comparator_10_eq, comparator_11_lt);
  Pull_Resistor pull_resistor_14 (.node(comparator_11_lt));
  Pull_Resistor pull_resistor_15 (.node(comparator_11_gt));
  and and_10 (and_10_out, comparator_10_eq, comparator_11_gt);
  and and_11 (and_11_out, comparator_12_eq, comparator_13_lt);
  Pull_Resistor pull_resistor_16 (.node(comparator_13_lt));
  Pull_Resistor pull_resistor_17 (.node(comparator_13_gt));
  and and_12 (and_12_out, comparator_12_eq, comparator_13_gt);
  Pull_Resistor pull_resistor_18 (.node(comparator_14_eq));
  Pull_Resistor pull_resistor_19 (.node(comparator_15_eq));
  Pull_Resistor pull_resistor_20 (.node(IN_4));
  assign IN_4 = and_9_out ? FloorDownReq : 4'bz;  // Controlled_Buffer controlled_buffer_10
  assign IN_2 = and_10_out ? FloorDownReq : 4'bz;  // Controlled_Buffer controlled_buffer_11
  Pull_Resistor pull_resistor_21 (.node(IN_2));
  assign IN_2 = and_11_out ? FloorDownReq : 4'bz;  // Controlled_Buffer controlled_buffer_12
  Pull_Resistor pull_resistor_22 (.node(IN4));
  assign IN4 = and_12_out ? FloorDownReq : 4'bz;  // Controlled_Buffer controlled_buffer_13
  Pull_Resistor pull_resistor_23 (.node(IN_2));
  assign IN_2 = comparator_14_eq ? FloorDownReq : 4'bz;  // Controlled_Buffer controlled_buffer_14
  Pull_Resistor pull_resistor_24 (.node(IN_4));
  assign IN_4 = comparator_15_eq ? FloorDownReq : 4'bz;  // Controlled_Buffer controlled_buffer_15
  or or_2 (F1U_LED, F1U_L1, F1U_L3);
  or or_3 (F2U_LED, F2U_L1, F2U_L3);
  or or_4 (F3U_LED, F3U_L1, F3U_L3);
  or or_5 (F4U_LED, F4U_L1, F4U_L3);
  or or_6 (F5U_LED, F5U_L1, F5U_L3);
  or or_7 (F6U_LED, F6U_L1, F6U_L3);
  or or_8 (F7U_LED, F7U_L1, F7U_L3);
  or or_9 (F8U_LED, F8U_L1, F8U_L3);
  or or_10 (F2D_LED, F2D_L2, F2D_L4);
  or or_11 (F3D_LED, F3D_L2, F3D_L4);
  or or_12 (F4D_LED, F4D_L2, F4D_L4);
  or or_13 (F5D_LED, F5D_L2, F5D_L4);
  or or_14 (F6D_LED, F6D_L2, F6D_L4);
  or or_15 (F7D_LED, F7D_L2, F7D_L4);
  or or_16 (F8D_LED, F8D_L2, F8D_L4);
  or or_17 (F9D_LED, F9D_L2, F9D_L4);
  not not_4 (Moving, hasStopped);
  Comparator #(.width(4), .mode("unsigned")) comparator_16 (
    .a(Current_Floor), .b(Next_Floor), .gt(Direction));  // open: eq, lt

  // Other names for the same wires on the sheet: CLR = CLEAR; CurrentFloor[3:0] = Current_Floor;
  //   DestinationFloorOUT[3:0] = Next_Floor

  // Notes on the sheet:
  //   Input
  //   Counter Subcircuit
  //   Stop Mechanism
  //   Request Stacks and Read Mechanism
  //   Request Processing Unit
  //   Output
endmodule

module Up_Down_Counter (
  input  [3:0] Current_Floor,
  input  [3:0] Destination,
  output [3:0] Next_Floor,
  output Stop
);

  wire and_1_out, and_2_out, and_3_out, CLK, clock_1_out, comparator_1_eq, comparator_2_eq, comparator_4_gt,
       comparator_4_lt, comparator_5_eq, comparator_6_eq, comparator_7_eq, comparator_7_lt, comparator_8_eq,
       comparator_8_gt, comparator_9_eq, comparator_10_eq, controlled_buffer_5_out, d_ff_1_q, d_ff_2_q,
       d_ff_3_q, d_ff_4_q, d_ff_5_q, d_ff_6_q, d_ff_7_q, d_ff_9_q, d_ff_10_q, d_ff_11_q, not_1_out,
       not_2_out, not_3_out, not_4_out, not_5_out, not_6_out, not_8_out, not_10_out, not_11_out, not_12_out,
       not_13_out, not_14_out, not_15_out, not_16_out, not_17_out, or_2_out, or_3_out, pull_resistor_3_node,
       pull_resistor_8_node, pull_resistor_9_node;
  wire [3:0] adder_1_out, controlled_buffer_1_out, controlled_buffer_2_out, controlled_buffer_3_out,
       controlled_buffer_4_out, controlled_buffer_6_out, controlled_buffer_7_out, multiplexer_1_out,
       multiplexer_2_out, register_1_q, register_2_q, subtractor_1_out;

  Clock clock_1 (.out(clock_1_out));
  not not_1 (not_1_out, comparator_1_eq);
  Comparator #(.width(4), .mode("unsigned")) comparator_1 (
    .a(Current_Floor), .b(4'b0000), .eq(comparator_1_eq));  // open: gt, lt
  Pull_Resistor pull_resistor_1 (.node(comparator_1_eq));
  Comparator #(.width(4), .mode("unsigned")) comparator_2 (
    .a(Destination), .b(4'b0000), .eq(comparator_2_eq));  // open: gt, lt
  Pull_Resistor #(.pull(1)) pull_resistor_2 (.node(comparator_2_eq));
  Pull_Resistor #(.pull(1)) pull_resistor_3 (.node(pull_resistor_3_node));
  Comparator #(.width(4), .mode("unsigned")) comparator_3 (
    .a(Current_Floor), .b(Destination), .eq(pull_resistor_3_node));  // open: gt, lt
  D_Flip_Flop d_ff_1 (.clk(clock_1_out), .D(not_2_out), .Q(d_ff_1_q));  // open: Qn, preset, en, reset
  not not_2 (not_2_out, d_ff_1_q);
  not not_3 (not_3_out, comparator_2_eq);
  not not_4 (not_4_out, d_ff_2_q);
  Comparator #(.width(4), .mode("unsigned")) comparator_4 (
    .a(Current_Floor), .b(Destination), .gt(comparator_4_gt), .lt(comparator_4_lt));  // open: eq
  assign controlled_buffer_1_out = and_1_out ? Destination : 4'bz;  // Controlled_Buffer controlled_buffer_1
  Pull_Resistor pull_resistor_4 (.node(controlled_buffer_1_out));
  or or_1 (Stop, pull_resistor_3_node, comparator_2_eq);
  D_Flip_Flop d_ff_2 (.clk(d_ff_1_q), .D(not_4_out), .Q(d_ff_2_q));  // open: Qn, preset, en, reset
  assign controlled_buffer_2_out = and_2_out ? Destination : 4'bz;  // Controlled_Buffer controlled_buffer_2
  Pull_Resistor pull_resistor_5 (.node(controlled_buffer_2_out));
  and and_1 (and_1_out, not_3_out, comparator_4_lt, not_1_out);
  assign controlled_buffer_3_out = and_1_out ? Current_Floor : 4'bz;  // Controlled_Buffer controlled_buffer_3
  Pull_Resistor pull_resistor_6 (.node(controlled_buffer_3_out));
  D_Flip_Flop d_ff_3 (.clk(d_ff_2_q), .D(not_5_out), .Q(d_ff_3_q));  // open: Qn, preset, en, reset
  not not_5 (not_5_out, d_ff_3_q);
  and and_2 (and_2_out, not_3_out, comparator_4_gt, not_1_out);
  assign controlled_buffer_4_out = and_2_out ? Current_Floor : 4'bz;  // Controlled_Buffer controlled_buffer_4
  Pull_Resistor pull_resistor_7 (.node(controlled_buffer_4_out));
  assign controlled_buffer_5_out = and_3_out ? CLK : 1'bz;  // Controlled_Buffer controlled_buffer_5
  and and_3 (and_3_out, not_1_out, not_3_out);
  Multiplexer #(.width(4)) multiplexer_1 (
    .in0(controlled_buffer_3_out), .in1(controlled_buffer_6_out), .out(multiplexer_1_out),
    .sel(pull_resistor_8_node));  // open: en
  Comparator #(.width(4), .mode("unsigned")) comparator_5 (
    .a(register_1_q), .b(4'b0000), .eq(comparator_5_eq));  // open: gt, lt
  D_Flip_Flop d_ff_4 (.clk(d_ff_3_q), .D(not_6_out), .Q(d_ff_4_q));  // open: Qn, preset, en, reset
  not not_6 (not_6_out, d_ff_4_q);
  Multiplexer #(.width(4)) multiplexer_2 (
    .in0(controlled_buffer_4_out), .in1(controlled_buffer_7_out), .out(multiplexer_2_out),
    .sel(pull_resistor_9_node));  // open: en
  Register #(.width(4)) register_1 (
    .D(multiplexer_1_out), .Q(register_1_q), .clk(controlled_buffer_5_out), .clr(and_2_out));  // open: en
  Pull_Resistor pull_resistor_8 (.node(pull_resistor_8_node));
  not not_7 (pull_resistor_8_node, comparator_5_eq);
  Register #(.width(4)) register_2 (
    .D(multiplexer_2_out), .Q(register_2_q), .clk(controlled_buffer_5_out), .clr(and_1_out));  // open: en
  Comparator #(.width(4), .mode("unsigned")) comparator_6 (
    .a(register_2_q), .b(4'b0000), .eq(comparator_6_eq));  // open: gt, lt
  D_Flip_Flop d_ff_5 (.clk(d_ff_4_q), .D(not_8_out), .Q(d_ff_5_q));  // open: Qn, preset, en, reset
  not not_8 (not_8_out, d_ff_5_q);
  Pull_Resistor pull_resistor_9 (.node(pull_resistor_9_node));
  not not_9 (pull_resistor_9_node, comparator_6_eq);
  assign controlled_buffer_6_out = or_2_out ? adder_1_out : 4'bz;  // Controlled_Buffer controlled_buffer_6
  Adder #(.width(4)) adder_1 (.a(register_1_q), .b(4'b0001), .out(adder_1_out));  // open: cin, cout
  D_Flip_Flop d_ff_6 (.clk(d_ff_5_q), .D(not_10_out), .Q(d_ff_6_q));  // open: Qn, preset, en, reset
  not not_10 (not_10_out, d_ff_6_q);
  assign controlled_buffer_7_out = or_3_out ? subtractor_1_out : 4'bz;  // Controlled_Buffer controlled_buffer_7
  Subtractor #(.width(4)) subtractor_1 (.a(register_2_q), .b(4'b0001), .out(subtractor_1_out));  // open: bin, bout
  Comparator #(.width(4), .mode("unsigned")) comparator_7 (
    .a(adder_1_out), .b(controlled_buffer_1_out), .eq(comparator_7_eq), .lt(comparator_7_lt));  // open: gt
  D_Flip_Flop d_ff_7 (.clk(d_ff_6_q), .D(not_11_out), .Q(d_ff_7_q));  // open: Qn, preset, en, reset
  not not_11 (not_11_out, d_ff_7_q);
  Comparator #(.width(4), .mode("unsigned")) comparator_8 (
    .a(subtractor_1_out), .b(controlled_buffer_2_out), .gt(comparator_8_gt), .eq(comparator_8_eq));  // open: lt
  or or_2 (or_2_out, comparator_7_eq, comparator_7_lt);
  or or_3 (or_3_out, comparator_8_gt, comparator_8_eq);
  Hex_Digit_Display hex_digit_display_1 (.value(register_1_q));  // open: dp
  D_Flip_Flop d_ff_8 (.clk(d_ff_7_q), .D(not_12_out), .Q(CLK));  // open: Qn, preset, en, reset
  not not_12 (not_12_out, CLK);
  Hex_Digit_Display hex_digit_display_2 (.value(register_2_q));  // open: dp
  D_Flip_Flop d_ff_9 (.clk(CLK), .D(not_13_out), .Q(d_ff_9_q));  // open: Qn, preset, en, reset
  not not_13 (not_13_out, d_ff_9_q);
  Comparator #(.width(4), .mode("unsigned")) comparator_9 (
    .a(register_2_q), .b(4'b0000), .eq(comparator_9_eq));  // open: gt, lt
  not not_14 (not_14_out, comparator_9_eq);
  assign Next_Floor = not_14_out ? register_2_q : 4'bz;  // Controlled_Buffer controlled_buffer_8
  assign Next_Floor = not_15_out ? register_1_q : 4'bz;  // Controlled_Buffer controlled_buffer_9
  not not_15 (not_15_out, comparator_10_eq);
  Comparator #(.width(4), .mode("unsigned")) comparator_10 (
    .a(register_1_q), .b(4'b0000), .eq(comparator_10_eq));  // open: gt, lt
  D_Flip_Flop d_ff_10 (.clk(d_ff_9_q), .D(not_16_out), .Q(d_ff_10_q));  // open: Qn, preset, en, reset
  not not_16 (not_16_out, d_ff_10_q);
  D_Flip_Flop d_ff_11 (.clk(d_ff_10_q), .D(not_17_out), .Q(d_ff_11_q));  // open: Qn, preset, en, reset
  not not_17 (not_17_out, d_ff_11_q);

  // Notes on the sheet:
  //   Destination: pull=down
  //   Current_Floor: pull=down
  //   Down Counter
  //   Up Counter
endmodule

module RequestStackDescending (
  input  Pop,
  input  [3:0] Input,
  input  Clear,
  output [3:0] Output,
  output F1_LED,
  output F2_LED,
  output F3_LED,
  output F4_LED,
  output F5_LED,
  output F6_LED,
  output F7_LED,
  output F8_LED,
  output F9_LED
);

  wire decoder_1_out1, decoder_1_out2, decoder_1_out3, decoder_1_out4, decoder_1_out5, decoder_1_out6,
       decoder_1_out7, decoder_1_out8, decoder_1_out9, decoder_1_out10, decoder_1_out11, decoder_1_out12,
       decoder_1_out13, decoder_1_out14, decoder_1_out15, decoder_1_out16, decoder_1_out17, decoder_1_out18,
       or_1_out, or_2_out, or_3_out, or_4_out, or_5_out, or_6_out, or_7_out, or_8_out, or_9_out, undriven;
  wire [3:0] memcelldescending_1_nextout, memcelldescending_2_nextout, memcelldescending_2_output,
       memcelldescending_3_nextout, memcelldescending_3_output, memcelldescending_4_nextout,
       memcelldescending_4_output, memcelldescending_5_nextout, memcelldescending_5_output,
       memcelldescending_6_nextout, memcelldescending_6_output, memcelldescending_7_nextout,
       memcelldescending_7_output, memcelldescending_8_nextout, memcelldescending_8_output,
       memcelldescending_9_output, multiplexer_1_out, multiplexer_2_out, multiplexer_3_out,
       multiplexer_4_out, multiplexer_5_out, multiplexer_6_out, multiplexer_7_out, multiplexer_8_out,
       multiplexer_9_out;
  wire [4:0] timercircuit_1_output;

  Pull_Resistor pull_resistor_1 (.node(Pop));
  // Probe on Output
  IsButtonOn isbuttonon_1 (
    .in_1(Output), .F1(F1_LED), .F2(F2_LED), .F3(F3_LED), .F4(F4_LED), .F5(F5_LED), .F6(F6_LED), .F7(F7_LED),
    .F8(F8_LED), .F9(F9_LED));
  TimerCircuit timercircuit_1 (.Start(Pop), .Output(timercircuit_1_output));
  Multiplexer #(.width(4)) multiplexer_1 (
    .in0(Input), .in1(memcelldescending_2_output), .out(multiplexer_1_out), .sel(decoder_1_out2));  // open: en
  MemCellDescending memcelldescending_1 (
    .Output(Output), .In(multiplexer_1_out), .NextOut(memcelldescending_1_nextout), .CLEAR(or_1_out));
  or or_1 (or_1_out, Clear, decoder_1_out1);
  Decoder #(.select(5)) decoder_1 (
    .out1(decoder_1_out1), .out2(decoder_1_out2), .out3(decoder_1_out3), .out4(decoder_1_out4),
    .out5(decoder_1_out5), .out6(decoder_1_out6), .out7(decoder_1_out7), .out8(decoder_1_out8),
    .out9(decoder_1_out9), .out10(decoder_1_out10), .out11(decoder_1_out11), .out12(decoder_1_out12),
    .out13(decoder_1_out13), .out14(decoder_1_out14), .out15(decoder_1_out15), .out16(decoder_1_out16),
    .out17(decoder_1_out17), .out18(decoder_1_out18), .sel(timercircuit_1_output));  // open: out0, out19, out20, out21, out22, out23, out24, out25, out26, out27, out28, out29, out30, out31, en
  IsButtonOn isbuttonon_2 (
    .in_1(memcelldescending_2_output), .F1(F1_LED), .F2(F2_LED), .F3(F3_LED), .F4(F4_LED), .F5(F5_LED),
    .F6(F6_LED), .F7(F7_LED), .F8(F8_LED), .F9(F9_LED));
  Multiplexer #(.width(4)) multiplexer_2 (
    .in0(memcelldescending_1_nextout), .in1(memcelldescending_3_output), .out(multiplexer_2_out),
    .sel(decoder_1_out4));  // open: en
  MemCellDescending memcelldescending_2 (
    .Output(memcelldescending_2_output), .In(multiplexer_2_out), .NextOut(memcelldescending_2_nextout),
    .CLEAR(or_2_out));
  // Probe on memcelldescending_2_output
  or or_2 (or_2_out, Clear, decoder_1_out3);
  IsButtonOn isbuttonon_3 (
    .in_1(memcelldescending_3_output), .F1(F1_LED), .F2(F2_LED), .F3(F3_LED), .F4(F4_LED), .F5(F5_LED),
    .F6(F6_LED), .F7(F7_LED), .F8(F8_LED), .F9(F9_LED));
  Multiplexer #(.width(4)) multiplexer_3 (
    .in0(memcelldescending_2_nextout), .in1(memcelldescending_4_output), .out(multiplexer_3_out),
    .sel(decoder_1_out6), .en(undriven));
  MemCellDescending memcelldescending_3 (
    .Output(memcelldescending_3_output), .In(multiplexer_3_out), .NextOut(memcelldescending_3_nextout),
    .CLEAR(or_3_out));
  // Probe on memcelldescending_3_output
  or or_3 (or_3_out, Clear, decoder_1_out5);
  IsButtonOn isbuttonon_4 (
    .in_1(memcelldescending_4_output), .F1(F1_LED), .F2(F2_LED), .F3(F3_LED), .F4(F4_LED), .F5(F5_LED),
    .F6(F6_LED), .F7(F7_LED), .F8(F8_LED), .F9(F9_LED));
  Multiplexer #(.width(4)) multiplexer_4 (
    .in0(memcelldescending_3_nextout), .in1(memcelldescending_5_output), .out(multiplexer_4_out),
    .sel(decoder_1_out8));  // open: en
  MemCellDescending memcelldescending_4 (
    .Output(memcelldescending_4_output), .In(multiplexer_4_out), .NextOut(memcelldescending_4_nextout),
    .CLEAR(or_4_out));
  // Probe on memcelldescending_4_output
  or or_4 (or_4_out, Clear, decoder_1_out7);
  IsButtonOn isbuttonon_5 (
    .in_1(memcelldescending_5_output), .F1(F1_LED), .F2(F2_LED), .F3(F3_LED), .F4(F4_LED), .F5(F5_LED),
    .F6(F6_LED), .F7(F7_LED), .F8(F8_LED), .F9(F9_LED));
  Multiplexer #(.width(4)) multiplexer_5 (
    .in0(memcelldescending_4_nextout), .in1(memcelldescending_6_output), .out(multiplexer_5_out),
    .sel(decoder_1_out10));  // open: en
  MemCellDescending memcelldescending_5 (
    .Output(memcelldescending_5_output), .In(multiplexer_5_out), .NextOut(memcelldescending_5_nextout),
    .CLEAR(or_5_out));
  // Probe on memcelldescending_5_output
  or or_5 (or_5_out, Clear, decoder_1_out9);
  Multiplexer #(.width(4)) multiplexer_6 (
    .in0(memcelldescending_5_nextout), .in1(memcelldescending_7_output), .out(multiplexer_6_out),
    .sel(decoder_1_out12));  // open: en
  // Probe on memcelldescending_6_output
  IsButtonOn isbuttonon_6 (
    .in_1(memcelldescending_6_output), .F1(F1_LED), .F2(F2_LED), .F3(F3_LED), .F4(F4_LED), .F5(F5_LED),
    .F6(F6_LED), .F7(F7_LED), .F8(F8_LED), .F9(F9_LED));
  MemCellDescending memcelldescending_6 (
    .Output(memcelldescending_6_output), .In(multiplexer_6_out), .NextOut(memcelldescending_6_nextout),
    .CLEAR(or_6_out));
  or or_6 (or_6_out, Clear, decoder_1_out11);
  // Probe on memcelldescending_7_output
  IsButtonOn isbuttonon_7 (
    .in_1(memcelldescending_7_output), .F1(F1_LED), .F2(F2_LED), .F3(F3_LED), .F4(F4_LED), .F5(F5_LED),
    .F6(F6_LED), .F7(F7_LED), .F8(F8_LED), .F9(F9_LED));
  Multiplexer #(.width(4)) multiplexer_7 (
    .in0(memcelldescending_6_nextout), .in1(memcelldescending_8_output), .out(multiplexer_7_out),
    .sel(decoder_1_out14));  // open: en
  MemCellDescending memcelldescending_7 (
    .Output(memcelldescending_7_output), .In(multiplexer_7_out), .NextOut(memcelldescending_7_nextout),
    .CLEAR(or_7_out));
  or or_7 (or_7_out, Clear, decoder_1_out13);
  Multiplexer #(.width(4)) multiplexer_8 (
    .in0(memcelldescending_7_nextout), .in1(memcelldescending_9_output), .out(multiplexer_8_out),
    .sel(decoder_1_out16));  // open: en
  // Probe on memcelldescending_8_output
  IsButtonOn isbuttonon_8 (
    .in_1(memcelldescending_8_output), .F1(F1_LED), .F2(F2_LED), .F3(F3_LED), .F4(F4_LED), .F5(F5_LED),
    .F6(F6_LED), .F7(F7_LED), .F8(F8_LED), .F9(F9_LED));
  MemCellDescending memcelldescending_8 (
    .Output(memcelldescending_8_output), .In(multiplexer_8_out), .NextOut(memcelldescending_8_nextout),
    .CLEAR(or_8_out));
  or or_8 (or_8_out, Clear, decoder_1_out15);
  Multiplexer #(.width(4)) multiplexer_9 (
    .in0(memcelldescending_8_nextout), .in1(4'b0000), .out(multiplexer_9_out), .sel(decoder_1_out18));  // open: en
  MemCellDescending memcelldescending_9 (
    .Output(memcelldescending_9_output), .In(multiplexer_9_out), .CLEAR(or_9_out));  // open: NextOut
  // Probe on memcelldescending_9_output
  IsButtonOn isbuttonon_9 (
    .in_1(memcelldescending_9_output), .F1(F1_LED), .F2(F2_LED), .F3(F3_LED), .F4(F4_LED), .F5(F5_LED),
    .F6(F6_LED), .F7(F7_LED), .F8(F8_LED), .F9(F9_LED));
  or or_9 (or_9_out, Clear, decoder_1_out17);
  Pull_Resistor pull_resistor_2 (.node(F1_LED));
  Pull_Resistor pull_resistor_3 (.node(F2_LED));
  Pull_Resistor pull_resistor_4 (.node(F3_LED));
  Pull_Resistor pull_resistor_5 (.node(F4_LED));
  Pull_Resistor pull_resistor_6 (.node(F5_LED));
  Pull_Resistor pull_resistor_7 (.node(F6_LED));
  Pull_Resistor pull_resistor_8 (.node(F7_LED));
  Pull_Resistor pull_resistor_9 (.node(F8_LED));
  Pull_Resistor pull_resistor_10 (.node(F9_LED));

  // Other names for the same wires on the sheet: F1 = F1_LED; F2 = F2_LED; F3 = F3_LED; F4 = F4_LED; F5 = F5_LED;
  //   F6 = F6_LED; F7 = F7_LED; F8 = F8_LED; F9 = F9_LED

  // Notes on the sheet:
  //   Clear: pull=down
endmodule

module RequestStackAscending (
  input  Pop,
  input  [3:0] Input,
  input  Clear,
  output [3:0] Output,
  output F1_LED,
  output F2_LED,
  output F3_LED,
  output F4_LED,
  output F5_LED,
  output F6_LED,
  output F7_LED,
  output F8_LED,
  output F9_LED
);

  wire decoder_1_out1, decoder_1_out2, decoder_1_out3, decoder_1_out4, decoder_1_out5, decoder_1_out6,
       decoder_1_out7, decoder_1_out8, decoder_1_out9, decoder_1_out10, decoder_1_out11, decoder_1_out12,
       decoder_1_out13, decoder_1_out14, decoder_1_out15, decoder_1_out16, decoder_1_out17, decoder_1_out18,
       or_1_out, or_2_out, or_3_out, or_4_out, or_5_out, or_6_out, or_7_out, or_8_out, or_9_out, undriven;
  wire [3:0] memcellascending_1_nextout, memcellascending_2_nextout, memcellascending_2_output,
       memcellascending_3_nextout, memcellascending_3_output, memcellascending_4_nextout,
       memcellascending_4_output, memcellascending_5_nextout, memcellascending_5_output,
       memcellascending_6_nextout, memcellascending_6_output, memcellascending_7_nextout,
       memcellascending_7_output, memcellascending_8_nextout, memcellascending_8_output,
       memcellascending_9_output, multiplexer_1_out, multiplexer_2_out, multiplexer_3_out, multiplexer_4_out,
       multiplexer_5_out, multiplexer_6_out, multiplexer_7_out, multiplexer_8_out, multiplexer_9_out;
  wire [4:0] timercircuit_1_output;

  Pull_Resistor pull_resistor_1 (.node(Pop));
  // Probe on Output
  IsButtonOn isbuttonon_1 (
    .in_1(Output), .F1(F1_LED), .F2(F2_LED), .F3(F3_LED), .F4(F4_LED), .F5(F5_LED), .F6(F6_LED), .F7(F7_LED),
    .F8(F8_LED), .F9(F9_LED));
  TimerCircuit timercircuit_1 (.Start(Pop), .Output(timercircuit_1_output));
  Multiplexer #(.width(4)) multiplexer_1 (
    .in0(Input), .in1(memcellascending_2_output), .out(multiplexer_1_out), .sel(decoder_1_out2));  // open: en
  MemCellAscending memcellascending_1 (
    .Output(Output), .In(multiplexer_1_out), .NextOut(memcellascending_1_nextout), .CLEAR(or_1_out));
  or or_1 (or_1_out, Clear, decoder_1_out1);
  Decoder #(.select(5)) decoder_1 (
    .out1(decoder_1_out1), .out2(decoder_1_out2), .out3(decoder_1_out3), .out4(decoder_1_out4),
    .out5(decoder_1_out5), .out6(decoder_1_out6), .out7(decoder_1_out7), .out8(decoder_1_out8),
    .out9(decoder_1_out9), .out10(decoder_1_out10), .out11(decoder_1_out11), .out12(decoder_1_out12),
    .out13(decoder_1_out13), .out14(decoder_1_out14), .out15(decoder_1_out15), .out16(decoder_1_out16),
    .out17(decoder_1_out17), .out18(decoder_1_out18), .sel(timercircuit_1_output));  // open: out0, out19, out20, out21, out22, out23, out24, out25, out26, out27, out28, out29, out30, out31, en
  IsButtonOn isbuttonon_2 (
    .in_1(memcellascending_2_output), .F1(F1_LED), .F2(F2_LED), .F3(F3_LED), .F4(F4_LED), .F5(F5_LED),
    .F6(F6_LED), .F7(F7_LED), .F8(F8_LED), .F9(F9_LED));
  Multiplexer #(.width(4)) multiplexer_2 (
    .in0(memcellascending_1_nextout), .in1(memcellascending_3_output), .out(multiplexer_2_out),
    .sel(decoder_1_out4));  // open: en
  MemCellAscending memcellascending_2 (
    .Output(memcellascending_2_output), .In(multiplexer_2_out), .NextOut(memcellascending_2_nextout),
    .CLEAR(or_2_out));
  // Probe on memcellascending_2_output
  or or_2 (or_2_out, Clear, decoder_1_out3);
  IsButtonOn isbuttonon_3 (
    .in_1(memcellascending_3_output), .F1(F1_LED), .F2(F2_LED), .F3(F3_LED), .F4(F4_LED), .F5(F5_LED),
    .F6(F6_LED), .F7(F7_LED), .F8(F8_LED), .F9(F9_LED));
  Multiplexer #(.width(4)) multiplexer_3 (
    .in0(memcellascending_2_nextout), .in1(memcellascending_4_output), .out(multiplexer_3_out),
    .sel(decoder_1_out6), .en(undriven));
  MemCellAscending memcellascending_3 (
    .Output(memcellascending_3_output), .In(multiplexer_3_out), .NextOut(memcellascending_3_nextout),
    .CLEAR(or_3_out));
  // Probe on memcellascending_3_output
  or or_3 (or_3_out, Clear, decoder_1_out5);
  IsButtonOn isbuttonon_4 (
    .in_1(memcellascending_4_output), .F1(F1_LED), .F2(F2_LED), .F3(F3_LED), .F4(F4_LED), .F5(F5_LED),
    .F6(F6_LED), .F7(F7_LED), .F8(F8_LED), .F9(F9_LED));
  Multiplexer #(.width(4)) multiplexer_4 (
    .in0(memcellascending_3_nextout), .in1(memcellascending_5_output), .out(multiplexer_4_out),
    .sel(decoder_1_out8));  // open: en
  MemCellAscending memcellascending_4 (
    .Output(memcellascending_4_output), .In(multiplexer_4_out), .NextOut(memcellascending_4_nextout),
    .CLEAR(or_4_out));
  // Probe on memcellascending_4_output
  or or_4 (or_4_out, Clear, decoder_1_out7);
  IsButtonOn isbuttonon_5 (
    .in_1(memcellascending_5_output), .F1(F1_LED), .F2(F2_LED), .F3(F3_LED), .F4(F4_LED), .F5(F5_LED),
    .F6(F6_LED), .F7(F7_LED), .F8(F8_LED), .F9(F9_LED));
  Multiplexer #(.width(4)) multiplexer_5 (
    .in0(memcellascending_4_nextout), .in1(memcellascending_6_output), .out(multiplexer_5_out),
    .sel(decoder_1_out10));  // open: en
  MemCellAscending memcellascending_5 (
    .Output(memcellascending_5_output), .In(multiplexer_5_out), .NextOut(memcellascending_5_nextout),
    .CLEAR(or_5_out));
  // Probe on memcellascending_5_output
  or or_5 (or_5_out, Clear, decoder_1_out9);
  Multiplexer #(.width(4)) multiplexer_6 (
    .in0(memcellascending_5_nextout), .in1(memcellascending_7_output), .out(multiplexer_6_out),
    .sel(decoder_1_out12));  // open: en
  // Probe on memcellascending_6_output
  IsButtonOn isbuttonon_6 (
    .in_1(memcellascending_6_output), .F1(F1_LED), .F2(F2_LED), .F3(F3_LED), .F4(F4_LED), .F5(F5_LED),
    .F6(F6_LED), .F7(F7_LED), .F8(F8_LED), .F9(F9_LED));
  MemCellAscending memcellascending_6 (
    .Output(memcellascending_6_output), .In(multiplexer_6_out), .NextOut(memcellascending_6_nextout),
    .CLEAR(or_6_out));
  or or_6 (or_6_out, Clear, decoder_1_out11);
  // Probe on memcellascending_7_output
  IsButtonOn isbuttonon_7 (
    .in_1(memcellascending_7_output), .F1(F1_LED), .F2(F2_LED), .F3(F3_LED), .F4(F4_LED), .F5(F5_LED),
    .F6(F6_LED), .F7(F7_LED), .F8(F8_LED), .F9(F9_LED));
  Multiplexer #(.width(4)) multiplexer_7 (
    .in0(memcellascending_6_nextout), .in1(memcellascending_8_output), .out(multiplexer_7_out),
    .sel(decoder_1_out14));  // open: en
  MemCellAscending memcellascending_7 (
    .Output(memcellascending_7_output), .In(multiplexer_7_out), .NextOut(memcellascending_7_nextout),
    .CLEAR(or_7_out));
  or or_7 (or_7_out, Clear, decoder_1_out13);
  Multiplexer #(.width(4)) multiplexer_8 (
    .in0(memcellascending_7_nextout), .in1(memcellascending_9_output), .out(multiplexer_8_out),
    .sel(decoder_1_out16));  // open: en
  // Probe on memcellascending_8_output
  IsButtonOn isbuttonon_8 (
    .in_1(memcellascending_8_output), .F1(F1_LED), .F2(F2_LED), .F3(F3_LED), .F4(F4_LED), .F5(F5_LED),
    .F6(F6_LED), .F7(F7_LED), .F8(F8_LED), .F9(F9_LED));
  MemCellAscending memcellascending_8 (
    .Output(memcellascending_8_output), .In(multiplexer_8_out), .NextOut(memcellascending_8_nextout),
    .CLEAR(or_8_out));
  or or_8 (or_8_out, Clear, decoder_1_out15);
  Multiplexer #(.width(4)) multiplexer_9 (
    .in0(memcellascending_8_nextout), .in1(4'b0000), .out(multiplexer_9_out), .sel(decoder_1_out18));  // open: en
  MemCellAscending memcellascending_9 (
    .Output(memcellascending_9_output), .In(multiplexer_9_out), .CLEAR(or_9_out));  // open: NextOut
  // Probe on memcellascending_9_output
  IsButtonOn isbuttonon_9 (
    .in_1(memcellascending_9_output), .F1(F1_LED), .F2(F2_LED), .F3(F3_LED), .F4(F4_LED), .F5(F5_LED),
    .F6(F6_LED), .F7(F7_LED), .F8(F8_LED), .F9(F9_LED));
  or or_9 (or_9_out, Clear, decoder_1_out17);
  Pull_Resistor pull_resistor_2 (.node(F1_LED));
  Pull_Resistor pull_resistor_3 (.node(F2_LED));
  Pull_Resistor pull_resistor_4 (.node(F3_LED));
  Pull_Resistor pull_resistor_5 (.node(F4_LED));
  Pull_Resistor pull_resistor_6 (.node(F5_LED));
  Pull_Resistor pull_resistor_7 (.node(F6_LED));
  Pull_Resistor pull_resistor_8 (.node(F7_LED));
  Pull_Resistor pull_resistor_9 (.node(F8_LED));
  Pull_Resistor pull_resistor_10 (.node(F9_LED));

  // Other names for the same wires on the sheet: F1 = F1_LED; F2 = F2_LED; F3 = F3_LED; F4 = F4_LED; F5 = F5_LED;
  //   F6 = F6_LED; F7 = F7_LED; F8 = F8_LED; F9 = F9_LED

  // Notes on the sheet:
  //   Clear: pull=down
endmodule

module MemCellDescending (
  input  [3:0] In,
  input  CLEAR,
  output [3:0] NextOut,
  output [3:0] Output
);

  wire and_1_out, and_2_out, clock_1_out, comparator_1_eq, comparator_2_gt, comparator_2_lt, comparator_3_eq,
       controlled_buffer_2_out, not_1_out, not_2_out, not_3_out, not_4_out, or_1_out;
  wire [3:0] controlled_buffer_1_out, controlled_buffer_3_out, register_2_q;

  Comparator #(.width(4), .mode("unsigned")) comparator_1 (.a(In), .b(4'b0000), .eq(comparator_1_eq));  // open: gt, lt
  assign controlled_buffer_1_out = or_1_out ? In : 4'bz;  // Controlled_Buffer controlled_buffer_1
  // Probe on controlled_buffer_1_out
  not not_1 (not_1_out, comparator_1_eq);
  or or_1 (or_1_out, comparator_3_eq, and_1_out);
  Pull_Resistor pull_resistor_1 (.node(In));
  Comparator #(.width(4), .mode("unsigned")) comparator_2 (
    .a(In), .b(Output), .gt(comparator_2_gt), .lt(comparator_2_lt));  // open: eq
  Register #(.width(4)) register_1 (
    .D(controlled_buffer_1_out), .Q(Output), .clk(controlled_buffer_2_out), .clr(CLEAR));  // open: en
  assign controlled_buffer_2_out = not_1_out ? clock_1_out : 1'bz;  // Controlled_Buffer controlled_buffer_2
  assign controlled_buffer_3_out = comparator_2_gt ? Output : 4'bz;  // Controlled_Buffer controlled_buffer_3
  Clock clock_1 (.out(clock_1_out));
  not not_2 (not_2_out, comparator_1_eq);
  and and_1 (and_1_out, not_2_out, comparator_2_gt);
  Register #(.width(4)) register_2 (
    .D(controlled_buffer_3_out), .Q(register_2_q), .clk(controlled_buffer_2_out), .clr(CLEAR));  // open: en
  Comparator #(.width(4), .mode("unsigned")) comparator_3 (
    .a(Output), .b(4'b0000), .eq(comparator_3_eq));  // open: gt, lt
  assign NextOut = and_2_out ? In : 4'bz;  // Controlled_Buffer controlled_buffer_4
  and and_2 (and_2_out, comparator_2_lt, not_3_out);
  not not_3 (not_3_out, comparator_3_eq);
  assign NextOut = not_4_out ? register_2_q : 4'bz;  // Controlled_Buffer controlled_buffer_5
  not not_4 (not_4_out, comparator_2_lt);
endmodule

module MemCellAscending (
  input  [3:0] In,
  input  CLEAR,
  output [3:0] NextOut,
  output [3:0] Output
);

  wire and_1_out, and_2_out, clock_1_out, comparator_1_eq, comparator_2_gt, comparator_2_lt, comparator_3_eq,
       controlled_buffer_2_out, not_1_out, not_2_out, not_3_out, not_4_out, or_1_out;
  wire [3:0] controlled_buffer_1_out, controlled_buffer_3_out, register_2_q;

  Comparator #(.width(4), .mode("unsigned")) comparator_1 (.a(In), .b(4'b0000), .eq(comparator_1_eq));  // open: gt, lt
  assign controlled_buffer_1_out = or_1_out ? In : 4'bz;  // Controlled_Buffer controlled_buffer_1
  // Probe on controlled_buffer_1_out
  not not_1 (not_1_out, comparator_1_eq);
  or or_1 (or_1_out, comparator_3_eq, and_1_out);
  Pull_Resistor pull_resistor_1 (.node(In));
  Comparator #(.width(4), .mode("unsigned")) comparator_2 (
    .a(In), .b(Output), .gt(comparator_2_gt), .lt(comparator_2_lt));  // open: eq
  Register #(.width(4)) register_1 (
    .D(controlled_buffer_1_out), .Q(Output), .clk(controlled_buffer_2_out), .clr(CLEAR));  // open: en
  assign controlled_buffer_2_out = not_1_out ? clock_1_out : 1'bz;  // Controlled_Buffer controlled_buffer_2
  assign controlled_buffer_3_out = comparator_2_lt ? Output : 4'bz;  // Controlled_Buffer controlled_buffer_3
  Clock clock_1 (.out(clock_1_out));
  not not_2 (not_2_out, comparator_1_eq);
  and and_1 (and_1_out, not_2_out, comparator_2_lt);
  Register #(.width(4)) register_2 (
    .D(controlled_buffer_3_out), .Q(register_2_q), .clk(controlled_buffer_2_out), .clr(CLEAR));  // open: en
  Comparator #(.width(4), .mode("unsigned")) comparator_3 (
    .a(Output), .b(4'b0000), .eq(comparator_3_eq));  // open: gt, lt
  assign NextOut = and_2_out ? In : 4'bz;  // Controlled_Buffer controlled_buffer_4
  and and_2 (and_2_out, comparator_2_gt, not_3_out);
  not not_3 (not_3_out, comparator_3_eq);
  assign NextOut = not_4_out ? register_2_q : 4'bz;  // Controlled_Buffer controlled_buffer_5
  not not_4 (not_4_out, comparator_2_gt);
endmodule

module TimerCircuit (
  input  Start,
  output [4:0] Output
);

  wire clock_1_out, comparator_1_eq, not_1_out, pull_resistor_1_node;

  not not_1 (not_1_out, Start);
  Comparator #(.width(5), .mode("unsigned")) comparator_1 (
    .a(Output), .b({5{1'b0}}), .eq(comparator_1_eq));  // open: gt, lt
  Clock clock_1 (.out(clock_1_out));
  Counter #(.width(5), .max('h12)) counter_1 (
    .Q(Output), .clk(clock_1_out), .clr(pull_resistor_1_node));  // open: load, D, count, carry
  Pull_Resistor pull_resistor_1 (.node(pull_resistor_1_node));
  assign pull_resistor_1_node = not_1_out ? comparator_1_eq : 1'bz;  // Controlled_Buffer controlled_buffer_1
endmodule

module Input_Handler (
  input  [3:0] Current_Floor,
  input  F1_COP,
  input  F2_COP,
  input  F3_COP,
  input  F4_COP,
  input  F5_COP,
  input  F6_COP,
  input  F7_COP,
  input  F8_COP,
  input  F9_COP,
  input  F1_UP,
  input  F2_UP,
  input  F2_DOWN,
  input  F3_UP,
  input  F3_DOWN,
  input  F4_UP,
  input  F4_DOWN,
  input  F5_UP,
  input  F5_DOWN,
  input  F6_UP,
  input  F6_DOWN,
  input  F7_UP,
  input  F7_DOWN,
  input  F8_UP,
  input  F8_DOWN,
  input  F9_DOWN,
  output [4:0] Request
);

  wire and_1_out, not_1_out, or_1_out, or_2_out;
  wire [3:0] controlled_buffer_1_out;
  wire [4:0] controlled_buffer_10_out, cop_unit_1_out_3;

  assign controlled_buffer_1_out = F1_COP ? 4'b0001 : 4'bz;  // Controlled_Buffer controlled_buffer_1
  assign controlled_buffer_1_out = F2_COP ? 4'b0010 : 4'bz;  // Controlled_Buffer controlled_buffer_2
  assign controlled_buffer_1_out = F3_COP ? 4'b0011 : 4'bz;  // Controlled_Buffer controlled_buffer_3
  assign controlled_buffer_1_out = F4_COP ? 4'b0100 : 4'bz;  // Controlled_Buffer controlled_buffer_4
  assign controlled_buffer_1_out = F5_COP ? 4'b0101 : 4'bz;  // Controlled_Buffer controlled_buffer_5
  assign controlled_buffer_1_out = F6_COP ? 4'b0110 : 4'bz;  // Controlled_Buffer controlled_buffer_6
  assign controlled_buffer_1_out = F7_COP ? 4'b0111 : 4'bz;  // Controlled_Buffer controlled_buffer_7
  assign controlled_buffer_1_out = F8_COP ? 4'b1000 : 4'bz;  // Controlled_Buffer controlled_buffer_8
  assign controlled_buffer_1_out = F9_COP ? 4'b1001 : 4'bz;  // Controlled_Buffer controlled_buffer_9
  assign controlled_buffer_10_out = F1_UP ? 5'b00001 : 5'bz;  // Controlled_Buffer controlled_buffer_10
  assign controlled_buffer_10_out = F2_UP ? 5'b00010 : 5'bz;  // Controlled_Buffer controlled_buffer_11
  assign controlled_buffer_10_out = F2_DOWN ? 5'b10010 : 5'bz;  // Controlled_Buffer controlled_buffer_12
  assign controlled_buffer_10_out = F3_UP ? 5'b00011 : 5'bz;  // Controlled_Buffer controlled_buffer_13
  assign controlled_buffer_10_out = F3_DOWN ? 5'b10011 : 5'bz;  // Controlled_Buffer controlled_buffer_14
  assign controlled_buffer_10_out = F4_UP ? 5'b00100 : 5'bz;  // Controlled_Buffer controlled_buffer_15
  assign controlled_buffer_10_out = F4_DOWN ? 5'b10100 : 5'bz;  // Controlled_Buffer controlled_buffer_16
  assign controlled_buffer_10_out = F5_UP ? 5'b00101 : 5'bz;  // Controlled_Buffer controlled_buffer_17
  assign controlled_buffer_10_out = F5_DOWN ? 5'b10101 : 5'bz;  // Controlled_Buffer controlled_buffer_18
  assign controlled_buffer_10_out = F6_UP ? 5'b00110 : 5'bz;  // Controlled_Buffer controlled_buffer_19
  assign controlled_buffer_10_out = F6_DOWN ? 5'b10110 : 5'bz;  // Controlled_Buffer controlled_buffer_20
  assign controlled_buffer_10_out = F7_UP ? 5'b00111 : 5'bz;  // Controlled_Buffer controlled_buffer_21
  assign controlled_buffer_10_out = F7_DOWN ? 5'b10111 : 5'bz;  // Controlled_Buffer controlled_buffer_22
  assign controlled_buffer_10_out = F8_UP ? 5'b01000 : 5'bz;  // Controlled_Buffer controlled_buffer_23
  assign controlled_buffer_10_out = F8_DOWN ? 5'b11000 : 5'bz;  // Controlled_Buffer controlled_buffer_24
  assign controlled_buffer_10_out = F9_DOWN ? 5'b11001 : 5'bz;  // Controlled_Buffer controlled_buffer_25
  COP_Unit cop_unit_1 (
    .Input_Request(controlled_buffer_1_out), .Current_Floor(Current_Floor), .out_3(cop_unit_1_out_3));
  Multiplexer #(.width(5)) multiplexer_1 (
    .in0(controlled_buffer_10_out), .in1(cop_unit_1_out_3), .out(Request), .sel(and_1_out));  // open: en
  and and_1 (and_1_out, or_2_out, not_1_out);
  not not_1 (not_1_out, or_1_out);
  Pull_Resistor pull_resistor_1 (.node(Request));
  or or_1 (or_1_out, F1_UP, F2_UP, F2_DOWN, F3_UP, F3_DOWN, F4_UP, F4_DOWN, F5_UP, F5_DOWN, F6_UP, F6_DOWN, F7_UP, F7_DOWN, F8_UP, F8_DOWN, F9_DOWN);
  or or_2 (or_2_out, F1_COP, F2_COP, F3_COP, F4_COP, F5_COP, F6_COP, F7_COP, F8_COP, F9_COP);

  // Other names for the same wires on the sheet: F1_C = F1_COP; F1_U = F1_UP; F2_C = F2_COP; F2_D = F2_DOWN;
  //   F2_U = F2_UP; F3_C = F3_COP; F3_D = F3_DOWN; F3_U = F3_UP; F4_C = F4_COP; F4_D = F4_DOWN; F4_U = F4_UP;
  //   F5_C = F5_COP; F5_D = F5_DOWN; F5_U = F5_UP; F6_C = F6_COP; F6_D = F6_DOWN; F6_U = F6_UP; F7_C = F7_COP;
  //   F7_D = F7_DOWN; F7_U = F7_UP; F8_C = F8_COP; F8_D = F8_DOWN; F8_U = F8_UP; F9_C = F9_COP; F9_D = F9_DOWN

  // Notes on the sheet:
  //   Request: pull=down
endmodule

module COP_Unit (
  input  [3:0] Input_Request,
  input  [3:0] Current_Floor,
  output [4:0] out_3
);

  wire and_1_out, comparator_1_eq, comparator_2_eq, comparator_3_gt, comparator_3_lt, not_1_out, not_2_out,
       or_1_out;
  wire [3:0] controlled_buffer_1_out;
  wire [4:0] multiplexer_1_out, multiplexer_2_out;

  assign controlled_buffer_1_out = not_1_out ? Input_Request : 4'bz;  // Controlled_Buffer controlled_buffer_1
  not not_1 (not_1_out, or_1_out);
  or or_1 (or_1_out, comparator_1_eq, comparator_2_eq);
  Comparator #(.width(4), .mode("unsigned")) comparator_1 (
    .a(Input_Request), .b(4'b0001), .eq(comparator_1_eq));  // open: gt, lt
  Comparator #(.width(4), .mode("unsigned")) comparator_2 (
    .a(Input_Request), .b(4'b1001), .eq(comparator_2_eq));  // open: gt, lt
  Comparator #(.width(4), .mode("unsigned")) comparator_3 (
    .a(controlled_buffer_1_out), .b(Current_Floor), .gt(comparator_3_gt), .lt(comparator_3_lt));  // open: eq
  Pull_Resistor pull_resistor_1 (.node(comparator_3_gt));
  Pull_Resistor pull_resistor_2 (.node(comparator_3_lt));
  Multiplexer #(.width(5)) multiplexer_1 (
    .in0({1'b0, Input_Request}), .in1({1'b1, Input_Request}), .out(multiplexer_1_out), .sel(and_1_out));  // open: en
  and and_1 (and_1_out, not_2_out, comparator_3_lt);
  not not_2 (not_2_out, comparator_3_gt);
  Multiplexer #(.width(5)) multiplexer_2 (
    .in0(5'b00001), .in1(5'b11001), .out(multiplexer_2_out), .sel(comparator_2_eq));  // open: en
  Multiplexer #(.width(5)) multiplexer_3 (
    .in0(multiplexer_1_out), .in1(multiplexer_2_out), .out(out_3), .sel(or_1_out));  // open: en

  // Notes on the sheet:
  //   Input_Request: pull=down
endmodule

module IsButtonOn (
  input  [3:0] in_1,
  output F1,
  output F2,
  output F3,
  output F4,
  output F5,
  output F6,
  output F7,
  output F8,
  output F9
);

  wire comparator_1_eq, comparator_2_eq, comparator_3_eq, comparator_4_eq, comparator_5_eq, comparator_6_eq,
       comparator_7_eq, comparator_8_eq, comparator_9_eq;

  assign F1 = comparator_1_eq ? comparator_1_eq : 1'bz;  // Controlled_Buffer controlled_buffer_1
  Comparator #(.width(4), .mode("unsigned")) comparator_1 (
    .a(in_1), .b(4'b0001), .eq(comparator_1_eq));  // open: gt, lt
  Comparator #(.width(4), .mode("unsigned")) comparator_2 (
    .a(in_1), .b(4'b0010), .eq(comparator_2_eq));  // open: gt, lt
  assign F2 = comparator_2_eq ? comparator_2_eq : 1'bz;  // Controlled_Buffer controlled_buffer_2
  Comparator #(.width(4), .mode("unsigned")) comparator_3 (
    .a(in_1), .b(4'b0011), .eq(comparator_3_eq));  // open: gt, lt
  assign F3 = comparator_3_eq ? comparator_3_eq : 1'bz;  // Controlled_Buffer controlled_buffer_3
  Comparator #(.width(4), .mode("unsigned")) comparator_4 (
    .a(in_1), .b(4'b0100), .eq(comparator_4_eq));  // open: gt, lt
  assign F4 = comparator_4_eq ? comparator_4_eq : 1'bz;  // Controlled_Buffer controlled_buffer_4
  Comparator #(.width(4), .mode("unsigned")) comparator_5 (
    .a(in_1), .b(4'b0101), .eq(comparator_5_eq));  // open: gt, lt
  assign F5 = comparator_5_eq ? comparator_5_eq : 1'bz;  // Controlled_Buffer controlled_buffer_5
  Comparator #(.width(4), .mode("unsigned")) comparator_6 (
    .a(in_1), .b(4'b0110), .eq(comparator_6_eq));  // open: gt, lt
  assign F6 = comparator_6_eq ? comparator_6_eq : 1'bz;  // Controlled_Buffer controlled_buffer_6
  assign F7 = comparator_7_eq ? comparator_7_eq : 1'bz;  // Controlled_Buffer controlled_buffer_7
  Comparator #(.width(4), .mode("unsigned")) comparator_7 (
    .a(in_1), .b(4'b0111), .eq(comparator_7_eq));  // open: gt, lt
  assign F8 = comparator_8_eq ? comparator_8_eq : 1'bz;  // Controlled_Buffer controlled_buffer_8
  Comparator #(.width(4), .mode("unsigned")) comparator_8 (
    .a(in_1), .b(4'b1000), .eq(comparator_8_eq));  // open: gt, lt
  assign F9 = comparator_9_eq ? comparator_9_eq : 1'bz;  // Controlled_Buffer controlled_buffer_9
  Comparator #(.width(4), .mode("unsigned")) comparator_9 (
    .a(in_1), .b(4'b1001), .eq(comparator_9_eq));  // open: gt, lt
endmodule

module DirectionDisplay (
  input  Direction__0___Up__1___Down,
  input  Moving,
  output [5:0] out_3,
  output [5:0] out_4,
  output [5:0] out_5,
  output [5:0] out_6,
  output [5:0] out_7
);

  Multiplexer #(.width(6)) multiplexer_1 (
    .in0(6'b001000), .in1(6'b000100), .out(out_7), .sel(Direction__0___Up__1___Down), .en(Moving));
  Multiplexer #(.width(6)) multiplexer_2 (
    .in0({6{1'b1}}), .in1({6{1'b1}}), .out(out_5), .sel(Direction__0___Up__1___Down), .en(Moving));
  Multiplexer #(.width(6)) multiplexer_3 (
    .in0(6'b010000), .in1(6'b000010), .out(out_6), .sel(Direction__0___Up__1___Down), .en(Moving));
  Multiplexer #(.width(6)) multiplexer_4 (
    .in0(6'b001000), .in1(6'b000100), .out(out_3), .sel(Direction__0___Up__1___Down), .en(Moving));
  Multiplexer #(.width(6)) multiplexer_5 (
    .in0(6'b010000), .in1(6'b000010), .out(out_4), .sel(Direction__0___Up__1___Down), .en(Moving));

  // Notes on the sheet:
  //   out_4: pull=down
  //   out_5: pull=down
  //   out_6: pull=down
  //   out_7: pull=down
  //   out_3: pull=down
endmodule

module Read_Sequencer (
  input  Start,
  input  Reset,
  output [2:0] Output
);

  wire clock_1_out, comparator_1_eq, not_1_out, or_1_out, pull_resistor_1_node, pull_resistor_2_node;

  not not_1 (not_1_out, Start);
  Comparator #(.width(3), .mode("unsigned")) comparator_1 (
    .a(Output), .b(3'b000), .eq(comparator_1_eq));  // open: gt, lt
  Pull_Resistor pull_resistor_1 (.node(pull_resistor_1_node));
  assign pull_resistor_1_node = Reset ? Reset : 1'bz;  // Controlled_Buffer controlled_buffer_1
  Clock clock_1 (.out(clock_1_out));
  Pull_Resistor pull_resistor_2 (.node(pull_resistor_2_node));
  assign pull_resistor_2_node = not_1_out ? comparator_1_eq : 1'bz;  // Controlled_Buffer controlled_buffer_2
  or or_1 (or_1_out, pull_resistor_2_node, pull_resistor_1_node);
  Counter #(.width(3), .max('h6)) counter_1 (
    .Q(Output), .clk(clock_1_out), .clr(or_1_out));  // open: load, D, count, carry
endmodule
